// Logisim project 306offlinePClFinal.circ as structural Verilog: 4 circuits, main circuit main
module main (
  input  [2:0] readReg,
  input  InstSpliter,
  input  [2:0] writeReg,
  input  in_4,
  input  in_5,
  input  [3:0] in_6,
  input  in_7,
  output [3:0] Count,
  output [3:0] out_9,
  output [3:0] out_10,
  output [3:0] out_11,
  output [3:0] out_12,
  output [3:0] out_13
);

  wire and_1_out, clock_1_out, control_1_alusrc, control_1_branch, control_1_jump, control_1_memread,
       control_1_memtoreg, control_1_memwrite, control_1_regdst, control_1_regwrite, mips_alu_4_bit_1_p4,
       not_1_out, or_1_out;
  wire [2:0] instspliter_1_inst_5_3, instspliter_1_inst_8_6, instspliter_1_inst_11_9, multiplexer_1_out,
       multiplexer_2_out, multiplexer_3_out;
  wire [3:0] adder_1_out, adder_2_out, control_1_aluop, mips_alu_4_bit_1_p5, multiplexer_4_out,
       multiplexer_6_out, multiplexer_7_out, multiplexer_8_out, ram_1_data;
  wire [15:0] rom_1_data;

  Counter #(.width(4), .max('hf), .trigger("falling")) counter_1 (
    .load(1'b1), .D(multiplexer_8_out), .count(1'b0), .Q(Count), .clk(clock_1_out), .clr(not_1_out));  // open: carry
  not not_1 (not_1_out, in_4);
  Adder #(.width(4)) adder_1 (.a(Count), .b(4'b0001), .out(adder_1_out));  // open: cin, cout
  ROM #(.addrWidth(4), .dataWidth(16)) rom_1 (.addr(Count), .data(rom_1_data), .sel(in_4));
  Clock clock_1 (.out(clock_1_out));
  InstSpliter instspliter_1 (
    .Inst(rom_1_data), .Inst_5_2(out_11), .Inst_5_3(instspliter_1_inst_5_3),
    .Inst_8_6(instspliter_1_inst_8_6), .Inst_11_9(instspliter_1_inst_11_9), .Inst_15_12(out_9));
  Multiplexer #(.width(3)) multiplexer_1 (
    .in0(writeReg), .in1(multiplexer_3_out), .out(multiplexer_1_out), .sel(in_5));  // open: en
  Multiplexer #(.width(3)) multiplexer_2 (
    .in0(readReg), .in1(instspliter_1_inst_11_9), .out(multiplexer_2_out), .sel(InstSpliter));  // open: en
  Multiplexer #(.width(3), .enable("false")) multiplexer_3 (
    .in0(instspliter_1_inst_8_6), .in1(instspliter_1_inst_5_3), .out(multiplexer_3_out),
    .sel(control_1_regdst));
  Control control_1 (
    .Inst_15_12(out_9), .RegDst(control_1_regdst), .ALUSrc(control_1_alusrc), .MemToReg(control_1_memtoreg),
    .RegWrite(control_1_regwrite), .MemRead(control_1_memread), .MemWrite(control_1_memwrite),
    .Branch(control_1_branch), .Jump(control_1_jump), .ALUop(control_1_aluop));
  RegisterFile RegFile (
    .readData1(out_10), .writeData(multiplexer_4_out), .regWrite(control_1_regwrite), .readData2(out_13),
    .Clk(clock_1_out), .writeReg(multiplexer_1_out), .readReg2(instspliter_1_inst_8_6),
    .readReg1(multiplexer_2_out));
  Multiplexer #(.width(4)) multiplexer_4 (
    .in0(in_6), .in1(multiplexer_6_out), .out(multiplexer_4_out), .sel(in_7));  // open: en
  Multiplexer #(.width(4), .enable("false")) multiplexer_5 (
    .in0(out_13), .in1(out_11), .out(out_12), .sel(control_1_alusrc));
  Adder #(.width(4)) adder_2 (.a(adder_1_out), .b(out_11), .out(adder_2_out));  // open: cin, cout
  // MIPS_ALU_4_bit mips_alu_4_bit_1: pin names not known; wires that end beside it: out_10, out_12, control_1_aluop, mips_alu_4_bit_1_p4, mips_alu_4_bit_1_p5
  Multiplexer #(.width(4), .enable("false")) multiplexer_6 (
    .in0(mips_alu_4_bit_1_p5), .in1(ram_1_data), .out(multiplexer_6_out), .sel(control_1_memtoreg));
  Multiplexer #(.width(4)) multiplexer_7 (
    .in0(adder_1_out), .in1(adder_2_out), .out(multiplexer_7_out), .sel(and_1_out));  // open: en
  and and_1 (and_1_out, control_1_branch, mips_alu_4_bit_1_p4);
  Multiplexer #(.width(4)) multiplexer_8 (
    .in0(multiplexer_7_out), .in1(rom_1_data[3:0]), .out(multiplexer_8_out), .sel(control_1_jump));  // open: en
  or or_1 (or_1_out, control_1_memwrite, control_1_memread);
  RAM #(.addrWidth(4), .dataWidth(4), .bus("separate")) ram_1 (
    .addr(mips_alu_4_bit_1_p5), .din(out_13), .data(ram_1_data), .str(control_1_memwrite), .sel(or_1_out),
    .clk(clock_1_out), .ld(control_1_memread));  // open: clr

  // Notes on the sheet:
  //   PC
  //   ROM/InstructionMem
  //   contents of rom_1 (hex, n*v repeats v):
  //   0 1050 2050 3290 4290 5050 6050 7050 8050 9050 a2a0 b050 c003
  //   control
  //   ALU
  //   writeData
endmodule

module RegisterFile (
  input  [3:0] writeData,
  input  regWrite,
  input  [2:0] readReg1,
  input  [2:0] writeReg,
  input  [2:0] readReg2,
  input  Clk,
  output [3:0] readData1,
  output [3:0] readData2
);

  wire and_1_out, and_2_out, and_3_out, and_4_out, and_5_out, and_6_out, and_7_out, and_8_out,
       decoder_1_out0, decoder_1_out1, decoder_1_out2, decoder_1_out3, decoder_1_out4, decoder_1_out5,
       decoder_1_out6, decoder_1_out7;
  wire [3:0] register_1_q, register_2_q, register_3_q, register_4_q, register_5_q, register_6_q,
       register_7_q, register_8_q;

  Decoder #(.select(3)) decoder_1 (
    .out0(decoder_1_out0), .out1(decoder_1_out1), .out2(decoder_1_out2), .out3(decoder_1_out3),
    .out4(decoder_1_out4), .out5(decoder_1_out5), .out6(decoder_1_out6), .out7(decoder_1_out7), .sel(writeReg));  // open: en
  and and_1 (and_1_out, regWrite, decoder_1_out0);
  and and_2 (and_2_out, regWrite, decoder_1_out1);
  and and_3 (and_3_out, regWrite, decoder_1_out2);
  and and_4 (and_4_out, regWrite, decoder_1_out3);
  Register #(.width(4)) register_1 (.D(writeData), .en(and_1_out), .Q(register_1_q), .clk(Clk), .clr(1'b0));
  Register #(.width(4)) register_2 (.D(writeData), .en(and_2_out), .Q(register_2_q), .clk(Clk), .clr(1'b0));
  Register #(.width(4)) register_3 (.D(writeData), .en(and_3_out), .Q(register_3_q), .clk(Clk), .clr(1'b0));
  Register #(.width(4)) register_4 (.D(writeData), .en(and_4_out), .Q(register_4_q), .clk(Clk), .clr(1'b0));
  and and_5 (and_5_out, regWrite, decoder_1_out4);
  and and_6 (and_6_out, regWrite, decoder_1_out5);
  and and_7 (and_7_out, regWrite, decoder_1_out6);
  and and_8 (and_8_out, regWrite, decoder_1_out7);
  Register #(.width(4)) register_5 (.D(writeData), .en(and_5_out), .Q(register_5_q), .clk(Clk), .clr(1'b0));
  Register #(.width(4)) register_6 (.D(writeData), .en(and_6_out), .Q(register_6_q), .clk(Clk), .clr(1'b0));
  Register #(.width(4)) register_7 (.D(writeData), .en(and_7_out), .Q(register_7_q), .clk(Clk), .clr(1'b0));
  Register #(.width(4)) register_8 (.D(writeData), .en(and_8_out), .Q(register_8_q), .clk(Clk), .clr(1'b0));
  Multiplexer #(.select(3), .width(4)) multiplexer_1 (
    .in0(register_1_q), .in1(register_2_q), .in2(register_3_q), .in3(register_4_q), .in4(register_5_q),
    .in5(register_6_q), .in6(register_7_q), .in7(register_8_q), .out(readData1), .sel(readReg1));  // open: en
  Multiplexer #(.select(3), .width(4)) multiplexer_2 (
    .in0(register_1_q), .in1(register_2_q), .in2(register_3_q), .in3(register_4_q), .in4(register_5_q),
    .in5(register_6_q), .in6(register_7_q), .in7(register_8_q), .out(readData2), .sel(readReg2));  // open: en
endmodule

module InstSpliter (
  input  [15:0] Inst,
  output [3:0] Inst_5_2,
  output [2:0] Inst_5_3,
  output [2:0] Inst_8_6,
  output [2:0] Inst_11_9,
  output [3:0] Inst_15_12
);


  assign Inst_5_2 = Inst[5:2];
  assign Inst_5_3 = Inst[5:3];
  assign Inst_8_6 = Inst[8:6];
  assign Inst_11_9 = Inst[11:9];
  assign Inst_15_12 = Inst[15:12];
endmodule

module Control (
  input  [3:0] Inst_15_12,
  output RegDst,
  output ALUSrc,
  output MemToReg,
  output RegWrite,
  output MemRead,
  output MemWrite,
  output Branch,
  output Jump,
  output [3:0] ALUop
);

  wire and_1_out, and_2_out, and_3_out, and_4_out, and_5_out, and_6_out, and_9_out, and_10_out, and_12_out,
       and_13_out, not_1_out, not_2_out, not_3_out, not_4_out;

  not not_1 (not_1_out, Inst_15_12[3]);
  not not_2 (not_2_out, Inst_15_12[2]);
  not not_3 (not_3_out, Inst_15_12[1]);
  not not_4 (not_4_out, Inst_15_12[0]);
  and and_1 (and_1_out, Inst_15_12[3], Inst_15_12[1]);
  and and_2 (and_2_out, Inst_15_12[2], Inst_15_12[1], Inst_15_12[0]);
  and and_3 (and_3_out, Inst_15_12[1], Inst_15_12[0]);
  and and_4 (and_4_out, not_1_out, not_2_out, not_3_out);
  and and_5 (and_5_out, not_1_out, not_2_out, not_4_out);
  or or_1 (ALUop[2], and_1_out, and_2_out);
  or or_2 (ALUop[0], and_4_out, and_5_out);
  and and_6 (and_6_out, not_1_out, not_2_out, Inst_15_12[1]);
  or or_3 (RegDst, Inst_15_12[3], Inst_15_12[2], not_3_out, not_4_out);
  and and_7 (MemWrite, not_1_out, not_3_out, not_4_out);
  and and_8 (MemRead, not_1_out, not_2_out, Inst_15_12[1], Inst_15_12[0]);
  or or_4 (ALUop[1], Inst_15_12[2], and_3_out, and_1_out);
  and and_9 (and_9_out, not_1_out, not_4_out);
  and and_10 (and_10_out, Inst_15_12[3], Inst_15_12[0]);
  and and_11 (MemToReg, not_1_out, not_2_out, Inst_15_12[1], Inst_15_12[0]);
  and and_12 (and_12_out, not_1_out, Inst_15_12[1]);
  and and_13 (and_13_out, not_2_out, not_3_out);
  and and_14 (Branch, Inst_15_12[3], Inst_15_12[1], not_4_out);
  and and_15 (Jump, Inst_15_12[3], Inst_15_12[2]);
  or or_5 (ALUSrc, and_9_out, and_10_out, and_6_out);
  or or_6 (RegWrite, and_12_out, Inst_15_12[0], and_13_out);

  assign ALUop[3] = 1'b0;
endmodule
