// Logisim project 306offlinePCl.circ as structural Verilog: 5 circuits, main circuit main
module main (
  input  in_1,
  input  [2:0] in_2,
  input  [3:0] in_3,
  input  in_4,
  output [3:0] Count,
  output [3:0] out_6,
  output [3:0] out_7,
  output [3:0] out_8,
  output out_9,
  output [3:0] out_10,
  output [2:0] out_11,
  output [3:0] out_12
);

  wire and_1_out, clock_1_out, control_1_alusrc, control_1_branch, control_1_jump, control_1_memread,
       control_1_memtoreg, control_1_memwrite, control_1_regdst, mips_alu_4_bit_1_p4, not_1_out, or_1_out;
  wire [2:0] instspliter_1_inst_5_3, instspliter_1_inst_8_6, instspliter_1_inst_11_9;
  wire [3:0] adder_1_out, adder_2_out, instspliter_1_inst_5_2, multiplexer_2_out, multiplexer_4_out,
       multiplexer_5_out, registerfile_1_readdata1, registerfile_1_readdata2;
  wire [15:0] rom_1_data;

  Counter #(.width(4), .max('hf), .trigger("falling")) counter_1 (
    .load(1'b1), .D(multiplexer_5_out), .count(1'b0), .Q(Count), .clk(clock_1_out), .clr(not_1_out));  // open: carry
  not not_1 (not_1_out, in_1);
  Adder #(.width(4)) adder_1 (.a(Count), .b(4'b0001), .out(adder_1_out));  // open: cin, cout
  Clock clock_1 (.out(clock_1_out));
  ROM #(.addrWidth(4), .dataWidth(16)) rom_1 (.addr(Count), .data(rom_1_data), .sel(in_1));
  InstSpliter instspliter_1 (
    .Inst(rom_1_data), .Inst_5_2(instspliter_1_inst_5_2), .Inst_5_3(instspliter_1_inst_5_3),
    .Inst_8_6(instspliter_1_inst_8_6), .Inst_11_9(instspliter_1_inst_11_9), .Inst_15_12(out_6));
  Multiplexer #(.width(3), .enable("false")) multiplexer_1 (
    .in0(instspliter_1_inst_8_6), .in1(instspliter_1_inst_5_3), .out(out_11), .sel(control_1_regdst));
  Control control_1 (
    .Inst_15_12(out_6), .RegDst(control_1_regdst), .ALUSrc(control_1_alusrc), .MemToReg(control_1_memtoreg),
    .RegWrite(out_9), .MemRead(control_1_memread), .MemWrite(control_1_memwrite), .Branch(control_1_branch),
    .Jump(control_1_jump), .ALUop(out_7));
  RegisterFile registerfile_1 (
    .readData1(registerfile_1_readdata1), .writeData(out_12), .regWrite(out_9),
    .readData2(registerfile_1_readdata2), .Clk(clock_1_out), .writeReg(out_11),
    .readReg2(instspliter_1_inst_8_6), .readReg1(instspliter_1_inst_11_9));
  Multiplexer #(.width(4), .enable("false")) multiplexer_2 (
    .in0(registerfile_1_readdata2), .in1(instspliter_1_inst_5_2), .out(multiplexer_2_out),
    .sel(control_1_alusrc));
  Adder #(.width(4)) adder_2 (.a(adder_1_out), .b(instspliter_1_inst_5_2), .out(adder_2_out));  // open: cin, cout
  // MIPS_ALU_4_bit mips_alu_4_bit_1: pin names not known; wires that end beside it: registerfile_1_readdata1, multiplexer_2_out, out_7, mips_alu_4_bit_1_p4, out_8
  Multiplexer #(.width(4), .enable("false")) multiplexer_3 (
    .in0(out_8), .in1(out_10), .out(out_12), .sel(control_1_memtoreg));
  Multiplexer #(.width(4), .enable("false")) multiplexer_4 (
    .in0(adder_1_out), .in1(adder_2_out), .out(multiplexer_4_out), .sel(and_1_out));
  and and_1 (and_1_out, control_1_branch, mips_alu_4_bit_1_p4);
  Multiplexer #(.width(4), .enable("false")) multiplexer_5 (
    .in0(multiplexer_4_out), .in1(rom_1_data[3:0]), .out(multiplexer_5_out), .sel(control_1_jump));
  or or_1 (or_1_out, control_1_memwrite, control_1_memread);
  RAM #(.addrWidth(4), .dataWidth(4), .bus("separate")) ram_1 (
    .addr(out_8), .din(registerfile_1_readdata2), .data(out_10), .str(control_1_memwrite), .sel(or_1_out),
    .clk(clock_1_out), .ld(control_1_memread));  // open: clr

  // Notes on the sheet:
  //   ROM/InstructionMem
  //   contents of rom_1 (hex, n*v repeats v):
  //   5050 5280 3450
  //   InstSpliter
  //   control
endmodule

module control (
  input  [3:0] in_1,
  output RegDst,
  output ALUSrc,
  output MemToReg,
  output RegWrite,
  output MemRead,
  output MemWrite,
  output Branch,
  output Jump,
  output [3:0] out_10
);

  wire and_1_out, and_2_out, and_3_out, and_4_out, and_5_out, and_9_out, and_10_out, not_1_out, not_2_out,
       not_3_out, not_4_out;

  not not_1 (not_1_out, in_1[3]);
  not not_2 (not_2_out, in_1[2]);
  not not_3 (not_3_out, in_1[1]);
  not not_4 (not_4_out, in_1[0]);
  and and_1 (and_1_out, in_1[3], in_1[1]);
  and and_2 (and_2_out, in_1[2], in_1[1], in_1[0]);
  and and_3 (and_3_out, in_1[1], in_1[0]);
  and and_4 (and_4_out, not_1_out, not_2_out, not_3_out);
  and and_5 (and_5_out, not_1_out, not_2_out, not_4_out);
  or or_1 (out_10[2], and_1_out, and_2_out);
  or or_2 (out_10[0], and_4_out, and_5_out);
  or or_3 (RegDst, in_1[3], in_1[2], not_3_out, not_4_out);
  and and_6 (MemWrite, not_1_out, not_3_out, not_4_out);
  and and_7 (MemRead, not_1_out, not_2_out, in_1[1], in_1[0]);
  or or_4 (out_10[1], in_1[2], and_3_out, and_1_out);
  or or_5 (ALUSrc, MemWrite, MemRead);
  and and_8 (MemToReg, not_1_out, not_2_out, in_1[1], in_1[0]);
  and and_9 (and_9_out, not_1_out, in_1[1]);
  and and_10 (and_10_out, not_2_out, not_3_out);
  and and_11 (Branch, in_1[3], in_1[1], not_4_out);
  and and_12 (Jump, in_1[3], in_1[2]);
  or or_6 (RegWrite, and_9_out, in_1[0], and_10_out);

  assign out_10[3] = 1'b0;
endmodule

module RegisterFile (
  input  [3:0] writeData,
  input  regWrite,
  input  [2:0] readReg1,
  input  [2:0] writeReg,
  input  [2:0] readReg2,
  input  Clk,
  output [3:0] readData1,
  output [3:0] readData2
);

  wire and_1_out, and_2_out, and_3_out, and_4_out, and_5_out, and_6_out, and_7_out, and_8_out,
       decoder_1_out0, decoder_1_out1, decoder_1_out2, decoder_1_out3, decoder_1_out4, decoder_1_out5,
       decoder_1_out6, decoder_1_out7;
  wire [3:0] register_1_q, register_2_q, register_3_q, register_4_q, register_5_q, register_6_q,
       register_7_q, register_8_q;

  Decoder #(.select(3), .enable("false")) decoder_1 (
    .out0(decoder_1_out0), .out1(decoder_1_out1), .out2(decoder_1_out2), .out3(decoder_1_out3),
    .out4(decoder_1_out4), .out5(decoder_1_out5), .out6(decoder_1_out6), .out7(decoder_1_out7), .sel(writeReg));
  and and_1 (and_1_out, regWrite, decoder_1_out0);
  and and_2 (and_2_out, regWrite, decoder_1_out1);
  and and_3 (and_3_out, regWrite, decoder_1_out2);
  and and_4 (and_4_out, regWrite, decoder_1_out3);
  Register #(.width(4)) register_1 (.D(writeData), .en(and_1_out), .Q(register_1_q), .clk(Clk), .clr(1'b0));
  Register #(.width(4)) register_2 (.D(writeData), .en(and_2_out), .Q(register_2_q), .clk(Clk), .clr(1'b0));
  Register #(.width(4)) register_3 (.D(writeData), .en(and_3_out), .Q(register_3_q), .clk(Clk), .clr(1'b0));
  Register #(.width(4)) register_4 (.D(writeData), .en(and_4_out), .Q(register_4_q), .clk(Clk), .clr(1'b0));
  and and_5 (and_5_out, regWrite, decoder_1_out4);
  and and_6 (and_6_out, regWrite, decoder_1_out5);
  and and_7 (and_7_out, regWrite, decoder_1_out6);
  and and_8 (and_8_out, regWrite, decoder_1_out7);
  Register #(.width(4)) register_5 (.D(writeData), .en(and_5_out), .Q(register_5_q), .clk(Clk), .clr(1'b0));
  Register #(.width(4)) register_6 (.D(writeData), .en(and_6_out), .Q(register_6_q), .clk(Clk), .clr(1'b0));
  Register #(.width(4)) register_7 (.D(writeData), .en(and_7_out), .Q(register_7_q), .clk(Clk), .clr(1'b0));
  Register #(.width(4)) register_8 (.D(writeData), .en(and_8_out), .Q(register_8_q), .clk(Clk), .clr(1'b0));
  Multiplexer #(.select(3), .width(4), .enable("false")) multiplexer_1 (
    .in0(register_1_q), .in1(register_2_q), .in2(register_3_q), .in3(register_4_q), .in4(register_5_q),
    .in5(register_6_q), .in6(register_7_q), .in7(register_8_q), .out(readData1), .sel(readReg1));
  Multiplexer #(.select(3), .width(4), .enable("false")) multiplexer_2 (
    .in0(register_1_q), .in1(register_2_q), .in2(register_3_q), .in3(register_4_q), .in4(register_5_q),
    .in5(register_6_q), .in6(register_7_q), .in7(register_8_q), .out(readData2), .sel(readReg2));
endmodule

module InstSpliter (
  input  [15:0] Inst,
  output [3:0] Inst_5_2,
  output [2:0] Inst_5_3,
  output [2:0] Inst_8_6,
  output [2:0] Inst_11_9,
  output [3:0] Inst_15_12
);


  assign Inst_5_2 = Inst[5:2];
  assign Inst_5_3 = Inst[5:3];
  assign Inst_8_6 = Inst[8:6];
  assign Inst_11_9 = Inst[11:9];
  assign Inst_15_12 = Inst[15:12];
endmodule

module Control (
  input  [3:0] Inst_15_12,
  output RegDst,
  output ALUSrc,
  output MemToReg,
  output RegWrite,
  output MemRead,
  output MemWrite,
  output Branch,
  output Jump,
  output [3:0] ALUop
);

  wire and_1_out, and_2_out, and_3_out, and_4_out, and_5_out, and_9_out, and_10_out, not_1_out, not_2_out,
       not_3_out, not_4_out;

  not not_1 (not_1_out, Inst_15_12[3]);
  not not_2 (not_2_out, Inst_15_12[2]);
  not not_3 (not_3_out, Inst_15_12[1]);
  not not_4 (not_4_out, Inst_15_12[0]);
  and and_1 (and_1_out, Inst_15_12[3], Inst_15_12[1]);
  and and_2 (and_2_out, Inst_15_12[2], Inst_15_12[1], Inst_15_12[0]);
  and and_3 (and_3_out, Inst_15_12[1], Inst_15_12[0]);
  and and_4 (and_4_out, not_1_out, not_2_out, not_3_out);
  and and_5 (and_5_out, not_1_out, not_2_out, not_4_out);
  or or_1 (ALUop[2], and_1_out, and_2_out);
  or or_2 (ALUop[0], and_4_out, and_5_out);
  or or_3 (RegDst, Inst_15_12[3], Inst_15_12[2], not_3_out, not_4_out);
  and and_6 (MemWrite, not_1_out, not_3_out, not_4_out);
  and and_7 (MemRead, not_1_out, not_2_out, Inst_15_12[1], Inst_15_12[0]);
  or or_4 (ALUop[1], Inst_15_12[2], and_3_out, and_1_out);
  or or_5 (ALUSrc, MemWrite, MemRead);
  and and_8 (MemToReg, not_1_out, not_2_out, Inst_15_12[1], Inst_15_12[0]);
  and and_9 (and_9_out, not_1_out, Inst_15_12[1]);
  and and_10 (and_10_out, not_2_out, not_3_out);
  and and_11 (Branch, Inst_15_12[3], Inst_15_12[1], not_4_out);
  and and_12 (Jump, Inst_15_12[3], Inst_15_12[2]);
  or or_6 (RegWrite, and_9_out, Inst_15_12[0], and_10_out);

  assign ALUop[3] = 1'b0;
endmodule
