// Logisim project PC.circ as structural Verilog: 4 circuits, main circuit RegisterFile
module main (
  input  in_1,
  output [3:0] out_2
);

  wire and_1_out, clock_1_out, Control_alusrc, Control_branch, Control_memread, Control_memtoreg,
       Control_memwrite, Control_regdst, Control_regwrite, mips_alu_4_bit_1_p4, not_1_out;
  wire [2:0] InstSpliter_inst_5_3, InstSpliter_inst_8_6, InstSpliter_inst_11_9, multiplexer_1_out;
  wire [3:0] adder_1_out, adder_2_out, Control_aluop, InstSpliter_inst_5_2, InstSpliter_inst_15_12,
       mips_alu_4_bit_1_p5, multiplexer_2_out, multiplexer_3_out, multiplexer_4_out, ram_1_data,
       RegFile_readdata1, RegFile_readdata2;
  wire [15:0] rom_1_data;

  Counter #(.width(4), .max('hf), .trigger("falling")) counter_1 (
    .load(1'b1), .D(multiplexer_4_out), .count(1'b0), .Q(out_2), .clk(clock_1_out), .clr(not_1_out));  // open: carry
  not not_1 (not_1_out, in_1);
  Clock clock_1 (.out(clock_1_out));
  ROM #(.addrWidth(4), .dataWidth(16)) rom_1 (.addr(out_2), .data(rom_1_data), .sel(in_1));
  Adder #(.width(4)) adder_1 (.a(out_2), .b(4'b0001), .out(adder_1_out));  // open: cin, cout
  InstSpliter InstSpliter (
    .Inst(rom_1_data), .Inst_5_2(InstSpliter_inst_5_2), .Inst_5_3(InstSpliter_inst_5_3),
    .Inst_8_6(InstSpliter_inst_8_6), .Inst_11_9(InstSpliter_inst_11_9), .Inst_15_12(InstSpliter_inst_15_12));
  Multiplexer #(.width(3)) multiplexer_1 (
    .in0(InstSpliter_inst_8_6), .in1(InstSpliter_inst_5_3), .out(multiplexer_1_out), .sel(Control_regdst));  // open: en
  Control Control (
    .RegDst(Control_regdst), .Branch(Control_branch), .MemRead(Control_memread), .MemtoReg(Control_memtoreg),
    .MemWrite(Control_memwrite), .ALUOp(Control_aluop), .ALUSrc(Control_alusrc), .RegWrite(Control_regwrite),
    .Inst_15_12(InstSpliter_inst_15_12));
  RegisterFile RegFile (
    .readData1(RegFile_readdata1), .writeData(multiplexer_3_out), .regWrite(Control_regwrite),
    .readData2(RegFile_readdata2), .writeReg(multiplexer_1_out), .readReg2(InstSpliter_inst_8_6),
    .readReg1(InstSpliter_inst_11_9), .Clk(clock_1_out));
  Multiplexer #(.width(4)) multiplexer_2 (
    .in0(RegFile_readdata2), .in1(InstSpliter_inst_5_2), .out(multiplexer_2_out), .sel(Control_alusrc));  // open: en
  Adder #(.width(4)) adder_2 (.a(adder_1_out), .b(InstSpliter_inst_5_2), .out(adder_2_out));  // open: cin, cout
  // MIPS_ALU_4_bit mips_alu_4_bit_1: pin names not known; wires that end beside it: RegFile_readdata1, multiplexer_2_out, Control_aluop, mips_alu_4_bit_1_p4, mips_alu_4_bit_1_p5
  Multiplexer #(.width(4)) multiplexer_3 (
    .in0(mips_alu_4_bit_1_p5), .in1(ram_1_data), .out(multiplexer_3_out), .sel(Control_memtoreg));  // open: en
  and and_1 (and_1_out, Control_branch, mips_alu_4_bit_1_p4);
  Multiplexer #(.width(4)) multiplexer_4 (
    .in0(adder_1_out), .in1(adder_2_out), .out(multiplexer_4_out), .sel(and_1_out));  // open: en
  RAM #(.addrWidth(4), .dataWidth(4), .bus("separate")) ram_1 (
    .addr(mips_alu_4_bit_1_p5), .din(RegFile_readdata2), .data(ram_1_data), .str(Control_memwrite),
    .clk(clock_1_out), .ld(Control_memread));  // open: sel, clr

  // Notes on the sheet:
  //   contents of rom_1 (hex, n*v repeats v):
  //   5060 3868 3 4
endmodule

module RegisterFile (
  input  [3:0] writeData,
  input  regWrite,
  input  [2:0] readReg1,
  input  [2:0] writeReg,
  input  [2:0] readReg2,
  input  Clk,
  output [3:0] readData1,
  output [3:0] readData2
);

  wire and_1_out, and_2_out, and_3_out, and_4_out, and_5_out, and_6_out, and_7_out, and_8_out,
       decoder_1_out0, decoder_1_out1, decoder_1_out2, decoder_1_out3, decoder_1_out4, decoder_1_out5,
       decoder_1_out6, decoder_1_out7;
  wire [3:0] register_1_q, register_2_q, register_3_q, register_4_q, register_5_q, register_6_q,
       register_7_q, register_8_q;

  Decoder #(.select(3)) decoder_1 (
    .out0(decoder_1_out0), .out1(decoder_1_out1), .out2(decoder_1_out2), .out3(decoder_1_out3),
    .out4(decoder_1_out4), .out5(decoder_1_out5), .out6(decoder_1_out6), .out7(decoder_1_out7), .sel(writeReg));  // open: en
  and and_1 (and_1_out, regWrite, decoder_1_out0);
  and and_2 (and_2_out, regWrite, decoder_1_out1);
  and and_3 (and_3_out, regWrite, decoder_1_out2);
  and and_4 (and_4_out, regWrite, decoder_1_out3);
  Register #(.width(4)) register_1 (.D(writeData), .en(and_1_out), .Q(register_1_q), .clk(Clk), .clr(1'b0));
  Register #(.width(4)) register_2 (.D(writeData), .en(and_2_out), .Q(register_2_q), .clk(Clk), .clr(1'b0));
  Register #(.width(4)) register_3 (.D(writeData), .en(and_3_out), .Q(register_3_q), .clk(Clk), .clr(1'b0));
  Register #(.width(4)) register_4 (.D(writeData), .en(and_4_out), .Q(register_4_q), .clk(Clk), .clr(1'b0));
  and and_5 (and_5_out, regWrite, decoder_1_out4);
  and and_6 (and_6_out, regWrite, decoder_1_out5);
  and and_7 (and_7_out, regWrite, decoder_1_out6);
  and and_8 (and_8_out, regWrite, decoder_1_out7);
  Register #(.width(4)) register_5 (.D(writeData), .en(and_5_out), .Q(register_5_q), .clk(Clk), .clr(1'b0));
  Register #(.width(4)) register_6 (.D(writeData), .en(and_6_out), .Q(register_6_q), .clk(Clk), .clr(1'b0));
  Register #(.width(4)) register_7 (.D(writeData), .en(and_7_out), .Q(register_7_q), .clk(Clk), .clr(1'b0));
  Register #(.width(4)) register_8 (.D(writeData), .en(and_8_out), .Q(register_8_q), .clk(Clk), .clr(1'b0));
  Multiplexer #(.select(3), .width(4)) multiplexer_1 (
    .in0(register_1_q), .in1(register_2_q), .in2(register_3_q), .in3(register_4_q), .in4(register_5_q),
    .in5(register_6_q), .in6(register_7_q), .in7(register_8_q), .out(readData1), .sel(readReg1));  // open: en
  Multiplexer #(.select(3), .width(4)) multiplexer_2 (
    .in0(register_1_q), .in1(register_2_q), .in2(register_3_q), .in3(register_4_q), .in4(register_5_q),
    .in5(register_6_q), .in6(register_7_q), .in7(register_8_q), .out(readData2), .sel(readReg2));  // open: en
endmodule

module InstSpliter (
  input  [15:0] Inst,
  output [3:0] Inst_5_2,
  output [2:0] Inst_5_3,
  output [2:0] Inst_8_6,
  output [2:0] Inst_11_9,
  output [3:0] Inst_15_12
);


  assign Inst_5_2 = Inst[5:2];
  assign Inst_5_3 = Inst[5:3];
  assign Inst_8_6 = Inst[8:6];
  assign Inst_11_9 = Inst[11:9];
  assign Inst_15_12 = Inst[15:12];
endmodule

module Control (
  input  [3:0] Inst_15_12,
  output RegDst,
  output Branch,
  output MemRead,
  output MemtoReg,
  output MemWrite,
  output [3:0] ALUOp,
  output ALUSrc,
  output RegWrite
);

  wire decoder_1_out0, decoder_1_out1, decoder_1_out5, decoder_1_out6, decoder_1_out7, decoder_1_out8,
       decoder_1_out9, decoder_1_out10, decoder_1_out11, decoder_1_out12, decoder_1_out13, decoder_1_out14,
       decoder_1_out15;

  Decoder #(.select(4)) decoder_1 (
    .out0(decoder_1_out0), .out1(decoder_1_out1), .out2(MemRead), .out3(MemWrite), .out4(Branch),
    .out5(decoder_1_out5), .out6(decoder_1_out6), .out7(decoder_1_out7), .out8(decoder_1_out8),
    .out9(decoder_1_out9), .out10(decoder_1_out10), .out11(decoder_1_out11), .out12(decoder_1_out12),
    .out13(decoder_1_out13), .out14(decoder_1_out14), .out15(decoder_1_out15), .sel(Inst_15_12));  // open: en
  or or_1 (RegDst, decoder_1_out11, decoder_1_out10, decoder_1_out8, decoder_1_out6);
  or or_2 (ALUOp[0], Branch, decoder_1_out6, decoder_1_out8);
  or or_3 (ALUOp[1], Branch, decoder_1_out6, decoder_1_out8, decoder_1_out5, decoder_1_out11);
  or or_4 (ALUSrc, decoder_1_out1, MemRead, MemWrite, decoder_1_out5, decoder_1_out8, decoder_1_out10);
  or or_5 (ALUOp[2], decoder_1_out1, decoder_1_out12);
  or or_6 (RegWrite, decoder_1_out1, MemRead, decoder_1_out5, decoder_1_out6, decoder_1_out8, decoder_1_out9, decoder_1_out10, decoder_1_out11, decoder_1_out12);

  assign ALUOp[3] = 1'b0;
  assign MemtoReg = MemRead;
endmodule
